// Digital circuit nna1.dig as structural Verilog
module nna1 (
  input  clk
);

  wire and_1_out, and_2_out, and_3_out, and_4_out, and_5_out, clock, decoder_1_out_0, decoder_2_out_0,
       decoder_2_out_1, decoder_2_out_2, decoder_3_out_0, decoder_3_out_1, decoder_3_out_2, decoder_3_out_3,
       not_1_out, not_2_out, notconnected_1_out, notconnected_2_out, notconnected_3_out, oflag_q, or_1_out,
       or_2_out, switchdt_1_p3;
  wire [0:0] or_3_out;
  wire [1:0] transgate_1_out2;
  wire [3:0] multiplexer_1_out, multiplexer_2_out, r0_q, r1_q, r2_q, r3_q, transgate_2_out2;
  wire [3:3] transgate_2_out1;
  wire [6:0] add_1_s, PC_q;
  wire [7:0] main_mem_d;

  Add #(.Bits(7)) add_1 (.a(PC_q), .b(7'b0000001), .c_i(1'b0), .s(add_1_s));  // open: c_o
  // SwitchDT switchdt_1: pin names not known; wires that end beside it: 1'b1, 1'b0, switchdt_1_p3
  Register #(.Bits(7), .isProgramCounter("true")) PC (.D(add_1_s), .C(clock), .en(1'b1), .Q(PC_q));
  // SwitchDT switchdt_2: pin names not known; wires that end beside it: clk, switchdt_1_p3, clock
  EEPROM #(.AddrBits(7), .isProgramMemory("true"), .Bits(8)) main_mem (
    .A(PC_q), .CS(1'b1), .WE(1'b0), .OE(1'b1), .D(main_mem_d));
  Decoder #(.Selector_Bits(4)) decoder_1 (
    .sel(main_mem_d[7:4]), .out_0(decoder_1_out_0));  // open: out_1, out_2, out_3, out_4, out_5, out_6, out_7, out_8, out_9, out_10, out_11, out_12, out_13, out_14, out_15
  Decoder #(.Selector_Bits(2)) decoder_2 (
    .sel(main_mem_d[3:2]), .out_0(decoder_2_out_0), .out_1(decoder_2_out_1), .out_2(decoder_2_out_2));  // open: out_3
  not not_1 (not_1_out, main_mem_d[0]);
  and and_1 (and_1_out, decoder_1_out_0, not_1_out, main_mem_d[1], decoder_2_out_0);
  and and_2 (and_2_out, decoder_2_out_1, decoder_1_out_0);
  and and_3 (and_3_out, decoder_1_out_0, decoder_2_out_2);
  and and_4 (and_4_out, decoder_1_out_0, main_mem_d[0], main_mem_d[1], decoder_2_out_0);
  Decoder #(.Selector_Bits(3)) decoder_3 (
    .sel({main_mem_d[1:0], or_3_out[0]}), .out_0(decoder_3_out_0), .out_1(decoder_3_out_1),
    .out_2(decoder_3_out_2), .out_3(decoder_3_out_3));  // open: out_4, out_5, out_6, out_7
  Register #(.Bits(4)) r0 (.D(transgate_2_out2), .C(clock), .en(decoder_3_out_0), .Q(r0_q));
  Register #(.Bits(4)) r1 (.D(transgate_2_out2), .C(clock), .en(decoder_3_out_1), .Q(r1_q));
  Register #(.Bits(4)) r2 (.D(transgate_2_out2), .C(clock), .en(decoder_3_out_2), .Q(r2_q));
  Register #(.Bits(4)) r3 (.D(transgate_2_out2), .C(clock), .en(decoder_3_out_3), .Q(r3_q));
  Multiplexer #(.Selector_Bits(2), .Bits(4)) multiplexer_1 (
    .sel(transgate_1_out2), .in_0(r0_q), .in_1(r1_q), .in_2(r2_q), .in_3(r3_q), .out(multiplexer_1_out));
  Multiplexer #(.Selector_Bits(2), .Bits(4)) multiplexer_2 (
    .sel(2'b00), .in_0(r0_q), .in_1(r1_q), .in_2(r2_q), .in_3(r3_q), .out(multiplexer_2_out));
  LED flf (.in(and_1_out));
  LED cfl (.in(and_4_out));
  LED shl (.in(and_2_out));
  LED shr (.in(and_3_out));
  TransGate #(.Bits(2)) transgate_1 (
    .A(or_2_out), .nA(notconnected_1_out), .out1(main_mem_d[1:0]), .out2(transgate_1_out2));
  // NotConnected on notconnected_1_out
  and and_5 (and_5_out, not_2_out, and_1_out);
  or or_1 (or_1_out, and_1_out, and_4_out);
  or or_2 (or_2_out, and_2_out, and_3_out);
  not not_2 (not_2_out, oflag_q);
  Register oflag (.D(and_5_out), .C(clock), .en(or_1_out), .Q(oflag_q));
  LED oflag_2 (.in(oflag_q));
  TransGate #(.Bits(4)) transgate_2 (
    .A(and_2_out), .nA(notconnected_2_out), .out1({transgate_2_out1[3], multiplexer_1_out[3:1]}),
    .out2(transgate_2_out2));
  // NotConnected on notconnected_2_out
  TransGate #(.Bits(4)) transgate_3 (
    .A(and_3_out), .nA(notconnected_3_out), .out1({multiplexer_1_out[2:0], transgate_2_out1[3]}),
    .out2(transgate_2_out2));
  // NotConnected on notconnected_3_out
  or or_3 (or_3_out[0], and_2_out, and_3_out);
  // also tied to GND on the sheet: transgate_2_out1[3]

  // Notes on the sheet:
  //   contents of main_mem (hex, n*v repeats v):
  //   0,2,3,2,2
  //   op decoder
  //   opcode
  //   opcode = 0
  //   arg1
  //   arg0
  //   arg0 = 0
  //   registers
  //   data in addr
  //   data in
  //   write
  //   data out 0
  //   out 0 addr
  //   data out 1
  //   out 1 addr
  //   shift left
  //   shift right
endmodule
