// Digital circuit bit-eater-v2.dig as structural Verilog
module bit_eater_v2 (
  input  clk
);

  wire add_1_c_o, add_2_c_o, and_1_out, and_2_out, and_12_out, and_13_out, and_14_out, and_15_out,
       and_16_out, and_17_out, and_18_out, and_19_out, and_20_out, and_25_out, and_26_out, and_27_out,
       and_28_out, and_30_out, bra, brk, cal, clf, comparator_1_eq, comparator_1_lt, d_ff_1_nq, dec,
       decoder_2_out_0, decoder_2_out_1, decoder_2_out_2, decoder_2_out_3, decoder_3_out_0, decoder_3_out_1,
       decoder_3_out_2, decoder_3_out_3, decoder_4_out_0, decoder_4_out_1, decoder_4_out_2, decoder_4_out_3,
       decoder_5_out_0, decoder_5_out_1, dread, dwrite, eq, flf, gt, inc, jmp, lih, lil, mco, mdb, mov, mpb,
       mrd, multiplexer_3_out, mwr, nop, not_1_out, not_2_out, not_3_out, not_4_out, not_5_out, not_6_out,
       not_7_out, not_8_out, not_9_out, not_10_out, not_11_out, not_12_out, not_13_out, not_14_out,
       not_15_out, not_16_out, not_17_out, not_18_out, oflag_out, or_1_out, or_2_out, or_3_out, or_4_out,
       or_5_out, or_6_out, or_7_out, or_8_out, or_9_out, or_10_out, or_11_out, or_12_out, or_13_out,
       or_14_out, or_15_out, or_16_out, or_17_out, pc_write, reset, reset_on_break_out, sin, sub_1_c_o,
       sub_2_c_o, xcycle, xcycle_next, \xor ;
  wire [1:0] and_3_out;
  wire [3:0] arg, co;
  wire [7:0] add_1_s, add_2_s, addrbus, db, mbus, pb, pc, pc_next, r1_q, r2_q, r3_q, regin, regout_arg0,
       regout_arg1, regout_r0, sub_1_s, sub_2_s, transgate_1_out2, transgate_8_out2, transgate_10_out2;
  wire [7:4] curop_q;

  // Probe on arg[3:2]
  // Probe on arg[1:0]
  Register #(.Bits(8)) curop (.D(mbus), .C(clk), .en(~xcycle), .Q({curop_q, arg}));
  Decoder #(.Selector_Bits(4)) decoder_1 (
    .sel(curop_q), .out_0(sin), .out_1(eq), .out_2(gt), .out_5(bra), .out_6(mco), .out_7(mwr), .out_8(mrd),
    .out_9(lil), .out_10(lih), .out_11(mov), .out_12(cal), .out_13(\xor ), .out_14(inc), .out_15(dec));  // open: out_3, out_4
  // Probe on arg
  Decoder #(.Selector_Bits(2)) decoder_2 (
    .sel(arg[3:2]), .out_0(decoder_2_out_0), .out_1(decoder_2_out_1), .out_2(decoder_2_out_2),
    .out_3(decoder_2_out_3));
  Decoder #(.Selector_Bits(2)) decoder_3 (
    .sel(arg[1:0]), .out_0(decoder_3_out_0), .out_1(decoder_3_out_1), .out_2(decoder_3_out_2),
    .out_3(decoder_3_out_3));
  and and_1 (and_1_out, mrd, ~xcycle);  // And
  or or_1 (or_1_out, and_1_out, brk, nop);
  or or_2 (or_2_out, lil, lih);
  and and_2 (and_2_out, sin, decoder_3_out_0);
  or or_3 (or_3_out, mwr, bra, gt, eq, flf, clf, jmp, or_1_out);
  and and_3 (and_3_out[1], arg[3], ~or_2_out);  // And
  and and_4 (and_3_out[0], arg[2], ~or_2_out);  // And
  and and_5 (nop, and_2_out, decoder_2_out_0);
  and and_6 (brk, and_2_out, decoder_2_out_1);
  and and_7 (flf, and_2_out, decoder_2_out_2);
  and and_8 (clf, and_2_out, decoder_2_out_3);
  and and_9 (jmp, decoder_3_out_1, sin);
  and and_10 (mpb, decoder_3_out_2, sin);
  and and_11 (mdb, decoder_3_out_3, sin);
  not not_1 (not_1_out, or_3_out);
  Decoder #(.Selector_Bits(2)) decoder_4 (
    .sel(and_3_out), .out_0(decoder_4_out_0), .out_1(decoder_4_out_1), .out_2(decoder_4_out_2),
    .out_3(decoder_4_out_3));
  TransGate #(.Bits(8)) transgate_1 (.A(not_4_out), .nA(reset), .out1(regin), .out2(transgate_1_out2));
  and and_12 (and_12_out, not_1_out, decoder_4_out_0);
  and and_13 (and_13_out, not_1_out, decoder_4_out_1);
  and and_14 (and_14_out, not_1_out, decoder_4_out_2);
  and and_15 (and_15_out, not_1_out, decoder_4_out_3);
  not not_2 (not_2_out, oflag_out);
  not not_3 (not_3_out, mov);
  TransGate #(.Bits(8)) transgate_2 (.A(mov), .nA(not_3_out), .out1(regout_arg1), .out2(regin));
  Add #(.Bits(8)) add_1 (.a(regout_arg0), .b({{6{1'b0}}, arg[1:0]}), .c_i(1'b0), .s(add_1_s), .c_o(add_1_c_o));
  Sub #(.Bits(8)) sub_1 (.a(regout_arg0), .b({{6{1'b0}}, arg[1:0]}), .c_i(1'b0), .s(sub_1_s), .c_o(sub_1_c_o));
  Comparator #(.Bits(8)) comparator_1 (
    .a(regout_arg0), .b(regout_arg1), .eq(comparator_1_eq), .lt(comparator_1_lt));  // open: gt
  not not_4 (not_4_out, reset);
  or or_4 (or_4_out, and_12_out, reset);
  or or_5 (or_5_out, and_13_out, reset);
  or or_6 (or_6_out, and_14_out, reset);
  or or_7 (or_7_out, and_15_out, reset);
  TransGate #(.Bits(8)) transgate_3 (.A(lil), .nA(not_5_out), .out1({regout_r0[7:4], arg}), .out2(regin));
  not not_5 (not_5_out, lil);
  TransGate #(.Bits(8)) transgate_4 (.A(lih), .nA(not_6_out), .out1({arg, regout_r0[3:0]}), .out2(regin));
  not not_6 (not_6_out, lih);
  and and_16 (and_16_out, flf, not_2_out);
  not not_7 (not_7_out, inc);
  TransGate #(.Bits(8)) transgate_5 (.A(inc), .nA(not_7_out), .out1(add_1_s), .out2(regin));
  and and_17 (and_17_out, add_1_c_o, inc);
  TransGate #(.Bits(8)) transgate_6 (.A(dec), .nA(not_8_out), .out1(sub_1_s), .out2(regin));
  and and_18 (and_18_out, sub_1_c_o, dec);
  and and_19 (and_19_out, eq, ~comparator_1_eq);  // And
  and and_20 (and_20_out, ~comparator_1_lt, gt);  // And
  not not_8 (not_8_out, dec);
  or or_8 (or_8_out, and_19_out, and_20_out);
  PullDown #(.Bits(8)) pulldown_1 (.out(transgate_1_out2));
  Register #(.Bits(8)) r0 (.D(transgate_1_out2), .C(clk), .en(or_4_out), .Q(regout_r0));
  Register #(.Bits(8)) r1 (.D(transgate_1_out2), .C(clk), .en(or_5_out), .Q(r1_q));
  Register #(.Bits(8)) r2 (.D(transgate_1_out2), .C(clk), .en(or_6_out), .Q(r2_q));
  Register #(.Bits(8)) r3 (.D(transgate_1_out2), .C(clk), .en(or_7_out), .Q(r3_q));
  Register #(.Bits(8)) u_pb (.D(regout_arg0), .C(clk), .en(mpb), .Q(pb));
  Register #(.Bits(8)) u_db (.D(regout_arg0), .C(clk), .en(mdb), .Q(db));
  Register #(.Bits(4)) u_co (.D(arg), .C(clk), .en(mco), .Q(co));
  or or_9 (or_9_out, and_16_out, and_17_out, and_18_out, or_8_out, and_28_out);
  // Probe on regout_r0
  // Probe on r1_q
  // Probe on r2_q
  // Probe on r3_q
  // Probe on pb
  // Probe on db
  // Probe on co
  or or_10 (or_10_out, reset, mpb);
  or or_11 (or_11_out, or_9_out, clf);
  Decoder #(.Selector_Bits(4)) decoder_5 (
    .sel(co), .out_0(decoder_5_out_0), .out_1(decoder_5_out_1));  // open: out_2, out_3, out_4, out_5, out_6, out_7, out_8, out_9, out_10, out_11, out_12, out_13, out_14, out_15
  or or_12 (or_12_out, xcycle, pc_write);
  Multiplexer #(.Selector_Bits(2), .Bits(8)) multiplexer_1 (
    .sel(arg[3:2]), .in_0(regout_r0), .in_1(r1_q), .in_2(r2_q), .in_3(r3_q), .out(regout_arg0));
  Multiplexer #(.Selector_Bits(2), .Bits(8)) multiplexer_2 (
    .sel(arg[1:0]), .in_0(regout_r0), .in_1(r1_q), .in_2(r2_q), .in_3(r3_q), .out(regout_arg1));
  CounterPreset #(.Bits(8), .isProgramCounter("true")) u_PC (
    .en(~xcycle), .C(clk), .dir(1'b0), .in(pc_next), .ld(pc_write), .clr(or_10_out), .out(pc));  // open: ovf
  Register oflag (.D(or_9_out), .C(clk), .en(or_11_out), .Q(oflag_out));
  DipSwitch reset_on_break (.out(reset_on_break_out));
  not not_9 (not_9_out, or_12_out);
  TransGate #(.Bits(8)) transgate_7 (.A(not_9_out), .nA(or_12_out), .out1(pc), .out2(addrbus));
  or or_13 (or_13_out, mrd, mwr);
  LED oflag_2 (.in(oflag_out));
  and and_21 (reset, reset_on_break_out, brk);
  and and_22 (xcycle_next, d_ff_1_nq, or_13_out);
  // Probe on mbus
  // Probe on addrbus
  and and_23 (dwrite, xcycle, mwr);
  and and_24 (dread, xcycle, mrd);
  or or_14 (or_14_out, dwrite, dread);
  TransGate #(.Bits(8)) transgate_8 (.A(or_14_out), .nA(not_10_out), .out1(db), .out2(transgate_8_out2));
  TransGate #(.Bits(8)) transgate_9 (.A(not_10_out), .nA(or_14_out), .out1(pb), .out2(transgate_8_out2));
  Add #(.Bits(8)) add_2 (.a(regout_arg0), .b(regout_arg1), .c_i(oflag_out), .s(add_2_s), .c_o(add_2_c_o));
  Sub #(.Bits(8)) sub_2 (.a(regout_arg0), .b(regout_arg1), .c_i(oflag_out), .s(sub_2_s), .c_o(sub_2_c_o));
  not not_10 (not_10_out, or_14_out);
  and and_25 (and_25_out, clk, dwrite);
  D_FF d_ff_1 (.D(xcycle_next), .C(~clk), .Q(xcycle), .nQ(d_ff_1_nq));
  TransGate #(.Bits(8)) transgate_10 (.A(decoder_5_out_0), .nA(not_11_out), .out1(add_2_s), .out2(transgate_10_out2));
  TransGate #(.Bits(8)) transgate_11 (.A(decoder_5_out_1), .nA(not_12_out), .out1(sub_2_s), .out2(transgate_10_out2));
  or or_15 (or_15_out, mwr, mrd);
  or or_16 (or_16_out, transgate_8_out2[5], transgate_8_out2[6], transgate_8_out2[7]);
  LED led_1 (.in(xcycle));
  not not_11 (not_11_out, decoder_5_out_0);
  not not_12 (not_12_out, decoder_5_out_1);
  and and_26 (and_26_out, xcycle, or_15_out);
  // Probe on pc
  TransGate #(.Bits(8)) transgate_12 (.A(dread), .nA(not_13_out), .out1(mbus), .out2(regin));
  not not_13 (not_13_out, dread);
  TransGate #(.Bits(8)) transgate_13 (.A(dwrite), .nA(not_14_out), .out1(regout_arg0), .out2(mbus));
  not not_14 (not_14_out, dwrite);
  EEPROM #(.AddrBits(13), .isProgramMemory("true"), .Bits(8)) eeprom_1 (
    .A({transgate_8_out2[4:0], addrbus}), .CS(~or_16_out), .WE(and_25_out), .OE(~dwrite), .D(mbus));
  TransGate #(.Bits(8)) transgate_14 (.A(cal), .nA(not_15_out), .out1(transgate_10_out2), .out2(regin));
  not not_15 (not_15_out, cal);
  TransGate #(.Bits(8)) transgate_15 (.A(and_26_out), .nA(not_16_out), .out1(regout_arg1), .out2(addrbus));
  not not_16 (not_16_out, and_26_out);
  or or_17 (or_17_out, bra, jmp);
  and and_27 (and_27_out, jmp, ~oflag_out);  // And
  and and_28 (and_28_out, cal, multiplexer_3_out);
  Multiplexer #(.Selector_Bits(4)) multiplexer_3 (
    .sel(co), .in_0(add_2_c_o), .in_1(sub_2_c_o), .in_2(1'b0), .in_3(1'b0), .in_4(1'b0), .in_5(1'b0),
    .in_6(1'b0), .in_7(1'b0), .in_8(1'b0), .in_9(1'b0), .in_10(1'b0), .in_11(1'b0), .in_12(1'b0),
    .in_13(1'b0), .in_14(1'b0), .in_15(1'b0), .out(multiplexer_3_out));
  and and_29 (pc_write, or_17_out, ~oflag_out);  // And
  not not_17 (not_17_out, and_27_out);
  TransGate #(.Bits(8)) transgate_16 (.A(and_27_out), .nA(not_17_out), .out1(regout_arg0), .out2(addrbus));
  and and_30 (and_30_out, bra, ~oflag_out);  // And
  Add #(.Bits(8)) add_3 (.a(addrbus), .b(8'h1), .c_i(1'b0), .s(pc_next));  // open: c_o
  TransGate #(.Bits(8)) transgate_17 (.A(and_30_out), .nA(not_18_out), .out1({pc[7:4], arg}), .out2(addrbus));
  not not_18 (not_18_out, and_30_out);

  // Other names for the same wires on the sheet: arg1[1:0] = arg[1:0]; arg0[1:0] = arg[3:2]; clock = clk

  // Notes on the sheet:
  //   clk: Hz: 200
  //   op decoder
  //   sin
  //   registers
  //   select r0 on lil,lih ops
  //   alu
  //   regin_addr
  //   lil lih
  //   flf clf mov
  //   write enable
  //   oflag
  //   pc,clock
  //   mwr, mrd
  //   main mem
  //   contents of eeprom_1 (hex, n*v repeats v):
  //   c,10,2f,54,ff,3c,2,65,13,2e,48,a9,12,2e,44,ff,e,7d,3e,15,2e,5c
  //   ,48,17,20,88,8,6f,da,3b,4,b,61,6,6,7,c,12,2e,34,2,44,14,2e,40
  //   ,3,61,6,6,7,c,13,2e,34,20,10,c,1
  //   jmp bra
  //   when bra,jmp put the target value on the addrbus and set pc to target+1
  //   because updates on next cycle
endmodule
